// Digital circuit part_c.dig as structural Verilog
module part_c (
  input  int_0,
  input  int_1,
  input  int_2,
  output out_0
);

  wire fgnfet_1_s, fgnfet_3_s, fgpfet_1_s, fgpfet_2_s, fgpfet_5_d;

  FGPFET fgpfet_1 (.G(int_0), .S(fgpfet_1_s), .D(1'b0));
  FGPFET fgpfet_2 (.G(int_2), .S(fgpfet_2_s), .D(1'b0));
  FGNFET fgnfet_1 (.G(int_1), .D(1'b1), .S(fgnfet_1_s));
  FGPFET fgpfet_3 (.G(int_1), .S(fgpfet_1_s), .D(1'b0));
  FGNFET fgnfet_2 (.G(int_0), .D(fgnfet_1_s), .S(fgpfet_1_s));
  FGPFET fgpfet_4 (.G(int_0), .S(fgpfet_2_s), .D(1'b0));
  FGNFET fgnfet_3 (.G(int_0), .D(1'b1), .S(fgnfet_3_s));
  FGNFET fgnfet_4 (.G(int_2), .D(fgnfet_3_s), .S(fgpfet_2_s));
  FGNFET fgnfet_5 (.G(fgpfet_1_s), .D(1'b1), .S(out_0));
  FGNFET fgnfet_6 (.G(fgpfet_2_s), .D(1'b1), .S(out_0));
  FGPFET fgpfet_5 (.G(fgpfet_2_s), .S(out_0), .D(fgpfet_5_d));
  FGPFET fgpfet_6 (.G(fgpfet_1_s), .S(fgpfet_5_d), .D(1'b0));
endmodule

/* Test case part_c_test:
int_0 int_1 int_2 out_0
   0     0     0     0
   0     0     1     0
   0     1     0     0
   0     1     1     0
   1     0     0     0
   1     0     1     1
   1     1     0     1
   1     1     1     1
*/
